# Fritzing sketch Flexit_SP30 (saved by Fritzing 0.9.3b)
breadboards: 1

parts:
  U2 = 817 Optocoupler [package=THT]
  U3 = 817 Optocoupler [package=THT]
  U4 = 817 Optocoupler [package=THT]
  R1 = Resistor [tolerance=±5% resistance=220 package=THT]
  R2 = Resistor [tolerance=±5% resistance=220 package=THT]
  R3 = Resistor [tolerance=±5% resistance=220 package=THT]
  R4 = Resistor [tolerance=±5% resistance=220 package=THT]
  R5 = Resistor [tolerance=±5% resistance=220 package=THT]
  R6 = Resistor [tolerance=±5% resistance=220 package=THT]
  U5 = 2-Channel 5v Relay Shield [package=relay-2ch5v10a]
  Z-uno_2_1 = Z-Uno 2.0
  U6 = RJ45 Jack [package=rj45-8]
  DS1 = DS18B20 1-Wire Temperature Sensor [part_number=DS18B20]
  DS2 = DS18B20 1-Wire Temperature Sensor [part_number=DS18B20]
  DS3 = DS18B20 1-Wire Temperature Sensor [part_number=DS18B20]
  DS4 = DS18B20 1-Wire Temperature Sensor [part_number=DS18B20]

nets:
  N1: U2.pin1, R2.Pin_0
  N2: U2.pin2, U3.pin2, U4.pin2, U5.K1-Off, U5.K2-Off, U6.7
  N3: U2.pin3, R4.Pin_1
  N4: U2.pin4, Z-uno_2_1.pin6
  N5: U3.pin1, R3.Pin_0
  N6: U3.pin3, R5.Pin_1
  N7: U3.pin4, Z-uno_2_1.pin5
  N8: U4.pin1, R1.Pin_0
  N9: U4.pin3, R6.Pin_1
  N10: U4.pin4, Z-uno_2_1.pin4
  N11: R1.Pin_1, U6.6
  N12: R2.Pin_1, U6.3
  GND: R4.Pin_0, R5.Pin_0, R6.Pin_0, U5.GND, Z-uno_2_1.GND#3, DS1.GND, DS2.GND, DS3.GND, DS4.GND
  VDD: U5.VCC, Z-uno_2_1.3V3#4, DS1.VDD, DS2.VDD, DS3.VDD, DS4.VDD
  N13: U5.IN1, Z-uno_2_1.ANT_U.FL, Z-uno_2_1.pin9
  N14: U5.IN2, Z-uno_2_1.pin10
  N15: U5.K1-On, U5.JD-GND
  N16: Z-uno_2_1.pin8, Z-uno_2_1.ANT
  N17: Z-uno_2_1.pin11, DS1.DQ, DS2.DQ, DS3.DQ, DS4.DQ
  N18: Z-uno_2_1.pin_22, Z-uno_2_1.3V3#44
  N19: Z-uno_2_1.pin_23, Z-uno_2_1.GND#43

custom parts:
  817 Optocoupler: A simple Sharp PC 817 optoisolator for non-demanding tasks www.hobbyspot.org
  2-Channel 5v Relay Shield: 2 Channel 5v Relay Shield w. 2x SPD-06VDC-SD-C
  Z-Uno 2.0: The Teensy is a complete USB-based microcontoller development system, in a very small footprint, capable of implementing many types of projects. All programming is done via the USB port. No special programmer is needed, only a standard micro-USB cable and a PC or Macintosh with a USB port. It has a USB keyboard/mouse/joystick emulation stack and can be programmed through Arduino IDE. Z-Uno is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
